# Fritzing sketch WaterTracker (saved by Fritzing 0.9.2b)
breadboards: 1

parts:
  パーツ1 = Arduino Micro (Rev3)  # not connected
  R1 = Resistor [tolerance=±5% resistance=10k package="2010 [SMD]"]
  J1 = Basic Force Sensing Resistor (FSR) [package=THT]

nets:
  N1: R1.Pin_1, J1.pin_0
